// Logisim project Notes_Circuit.circ as structural Verilog: 1 circuit, main circuit main
module main (
  input  in_1,
  input  in_2
);

  wire and_1_out, and_2_out, and_3_out, d_ff_1_qn, d_ff_2_qn, or_1_out;

  and and_1 (and_1_out, in_2, d_ff_2_qn);
  and and_2 (and_2_out, ~d_ff_2_qn, ~d_ff_2_qn, ~d_ff_2_qn);  // AND_Gate
  and and_3 (and_3_out, in_2, d_ff_1_qn, d_ff_1_qn);
  or or_1 (or_1_out, and_1_out, and_2_out);
  D_Flip_Flop d_ff_1 (.clk(in_1), .D(or_1_out), .Qn(d_ff_1_qn));  // open: Q, preset, en, reset
  D_Flip_Flop d_ff_2 (.clk(in_1), .D(and_3_out), .Qn(d_ff_2_qn));  // open: Q, preset, en, reset
endmodule
