// Logisim project circuit three.circ as structural Verilog: 1 circuit, main circuit main
module main (
  output out_1,
  output out_2
);

  not not_1 (out_1, out_2);
  not not_2 (out_2, out_1);
endmodule
